# Fritzing sketch moisture_sensor (saved by Fritzing 0.9.3b)

parts:
  U1 = NodeMCU V3.0
  Bauteil1 = Soil Moisture Sensor

nets:
  GND: U1.GND, Bauteil1.GND
  3V3: U1.3V3, Bauteil1.VCC
  N1: U1.A0, Bauteil1.SIG

custom parts:
  NodeMCU V3.0: ESP8266 based NodeMCU
